// Digital circuit 74382.dig as structural Verilog
// 4-Bit Arithmetic Logic Unit with ripple carry output
module _74382 (
  input  Cin,
  input  B0,
  input  A0,
  input  B1,
  input  A1,
  input  B2,
  input  A2,
  input  B3,
  input  A3,
  input  S0,
  input  S1,
  input  S2,
  input  VCC,
  input  GND,
  output CO,
  output OVR,
  output F0,
  output F1,
  output F2,
  output F3
);

  wire and_1_out, and_2_out, and_3_out, and_4_out, and_5_out, and_6_out, and_7_out, and_8_out, and_9_out,
       and_10_out, and_11_out, and_12_out, and_13_out, and_14_out, and_15_out, and_16_out, and_17_out,
       and_18_out, and_19_out, and_20_out, and_21_out, and_22_out, and_23_out, and_24_out, and_25_out,
       and_26_out, and_27_out, and_28_out, and_29_out, and_30_out, and_31_out, and_32_out, and_33_out,
       and_34_out, and_35_out, and_36_out, and_37_out, and_38_out, and_39_out, and_40_out, and_41_out,
       and_42_out, and_43_out, and_44_out, and_45_out, nand_1_out, nand_2_out, nand_3_out, nand_4_out,
       nand_5_out, nand_6_out, nor_1_out, nor_2_out, nor_3_out, nor_4_out, nor_5_out, nor_6_out, nor_7_out,
       nor_8_out, nor_9_out, nor_10_out, nor_11_out, nor_12_out, nor_13_out, nor_14_out, not_1_out,
       not_2_out, not_3_out, not_4_out, not_5_out, not_6_out, not_7_out, not_8_out, not_9_out, not_10_out,
       not_11_out, not_12_out, not_13_out, not_14_out;

  not not_1 (not_1_out, S0);
  not not_2 (not_2_out, S1);
  not not_3 (not_3_out, S2);
  not not_4 (not_4_out, not_1_out);
  not not_5 (not_5_out, not_2_out);
  not not_6 (not_6_out, not_3_out);
  not not_7 (not_7_out, B0);
  not not_8 (not_8_out, A0);
  not not_9 (not_9_out, B1);
  not not_10 (not_10_out, A1);
  not not_11 (not_11_out, B2);
  not not_12 (not_12_out, A2);
  not not_13 (not_13_out, B3);
  not not_14 (not_14_out, A3);
  nand nand_1 (nand_1_out, not_1_out, not_2_out);
  nand nand_2 (nand_2_out, not_2_out, not_3_out);
  nand nand_3 (nand_3_out, not_1_out, not_5_out);
  and and_1 (and_1_out, not_8_out, not_7_out, nand_3_out, nand_2_out);
  and and_2 (and_2_out, nand_1_out, nand_3_out, nand_4_out, not_7_out, A0);
  and and_3 (and_3_out, nand_2_out, nand_4_out, B0, not_8_out);
  and and_4 (and_4_out, not_8_out, not_7_out, nand_1_out, nand_4_out, nor_1_out);
  and and_5 (and_5_out, nand_2_out, nand_3_out, not_7_out, A0);
  and and_6 (and_6_out, nand_2_out, nand_3_out, B0, not_8_out);
  and and_7 (and_7_out, nand_1_out, nand_4_out, B0, A0);
  and and_8 (and_8_out, not_10_out, not_9_out, nand_3_out, nand_2_out);
  and and_9 (and_9_out, nand_1_out, nand_3_out, nand_4_out, not_9_out, A1);
  and and_10 (and_10_out, nand_2_out, nand_4_out, B1, not_10_out);
  and and_11 (and_11_out, not_10_out, not_9_out, nand_1_out, nand_4_out, nor_1_out);
  and and_12 (and_12_out, nand_2_out, nand_3_out, not_9_out, A1);
  and and_13 (and_13_out, nand_2_out, nand_3_out, B1, not_10_out);
  and and_14 (and_14_out, nand_1_out, nand_4_out, B1, A1);
  and and_15 (and_15_out, not_12_out, not_11_out, nand_3_out, nand_2_out);
  and and_16 (and_16_out, nand_1_out, nand_3_out, nand_4_out, not_11_out, A2);
  and and_17 (and_17_out, nand_2_out, nand_4_out, B2, not_12_out);
  and and_18 (and_18_out, not_12_out, not_11_out, nand_1_out, nand_4_out, nor_1_out);
  and and_19 (and_19_out, nand_2_out, nand_3_out, not_11_out, A2);
  and and_20 (and_20_out, nand_2_out, nand_3_out, B2, not_12_out);
  and and_21 (and_21_out, nand_1_out, nand_4_out, B2, A2);
  and and_22 (and_22_out, not_14_out, not_13_out, nand_3_out, nand_2_out);
  and and_23 (and_23_out, nand_1_out, nand_3_out, nand_4_out, not_13_out, A3);
  and and_24 (and_24_out, nand_2_out, nand_4_out, B3, not_14_out);
  and and_25 (and_25_out, not_14_out, not_13_out, nand_1_out, nand_4_out, nor_1_out);
  and and_26 (and_26_out, nand_2_out, nand_3_out, not_13_out, A3);
  and and_27 (and_27_out, nand_2_out, nand_3_out, B3, not_14_out);
  and and_28 (and_28_out, nand_1_out, nand_4_out, B3, A3);
  and and_29 (and_29_out, not_1_out, not_2_out);
  nand nand_4 (nand_4_out, not_4_out, not_5_out, not_3_out);
  and and_30 (and_30_out, not_2_out, not_6_out);
  and and_31 (and_31_out, not_1_out, not_6_out);
  nor nor_1 (nor_1_out, and_31_out, and_30_out);
  nor nor_2 (nor_2_out, and_1_out, and_2_out, and_3_out);
  nor nor_3 (nor_3_out, and_4_out, and_5_out, and_6_out, and_7_out);
  nor nor_4 (nor_4_out, and_8_out, and_9_out, and_10_out);
  nor nor_5 (nor_5_out, and_11_out, and_12_out, and_13_out, and_14_out);
  nor nor_6 (nor_6_out, and_15_out, and_16_out, and_17_out);
  nor nor_7 (nor_7_out, and_18_out, and_19_out, and_20_out, and_21_out);
  nor nor_8 (nor_8_out, and_22_out, and_23_out, and_24_out);
  nor nor_9 (nor_9_out, and_25_out, and_26_out, and_27_out, and_28_out);
  nor nor_10 (nor_10_out, and_29_out, not_6_out);
  and and_32 (and_32_out, Cin, nor_2_out, nor_10_out);
  and and_33 (and_33_out, nor_2_out, nor_3_out, nor_10_out);
  and and_34 (and_34_out, Cin, nor_2_out, nor_4_out, nor_10_out);
  and and_35 (and_35_out, nor_2_out, nor_4_out, nor_3_out, nor_10_out);
  and and_36 (and_36_out, nor_4_out, nor_5_out, nor_10_out);
  and and_37 (and_37_out, Cin, nor_2_out, nor_4_out, nor_6_out, nor_10_out);
  and and_38 (and_38_out, nor_2_out, nor_4_out, nor_6_out, nor_3_out, nor_10_out);
  and and_39 (and_39_out, nor_4_out, nor_6_out, nor_5_out, nor_10_out);
  and and_40 (and_40_out, nor_6_out, nor_7_out, nor_10_out);
  and and_41 (and_41_out, nor_2_out, nor_4_out, nor_6_out, nor_8_out, nor_3_out);
  and and_42 (and_42_out, nor_4_out, nor_6_out, nor_8_out, nor_5_out);
  and and_43 (and_43_out, nor_6_out, nor_8_out, nor_7_out);
  and and_44 (and_44_out, nor_8_out, nor_9_out);
  nand nand_5 (nand_5_out, Cin, nor_2_out, nor_4_out, nor_6_out, nor_8_out);
  nor nor_11 (nor_11_out, and_32_out, and_33_out);
  nor nor_12 (nor_12_out, and_37_out, and_38_out, and_39_out, and_40_out);
  PowerSupply powersupply_1 (.VDD(VCC), .GND(GND));
  nand nand_6 (nand_6_out, Cin, nor_10_out);
  nor nor_13 (nor_13_out, and_34_out, and_35_out, and_36_out);
  nor nor_14 (nor_14_out, and_41_out, and_42_out, and_43_out, and_44_out);
  xor xor_1 (F0, nand_6_out, nor_3_out);
  xor xor_2 (F1, nor_11_out, nor_5_out);
  and and_45 (and_45_out, nor_14_out, nand_5_out);
  nand nand_7 (CO, nor_14_out, nand_5_out);
  xor xor_3 (F2, nor_13_out, nor_7_out);
  xor xor_4 (OVR, nor_12_out, and_45_out);
  xor xor_5 (F3, nor_12_out, nor_9_out);

  // Notes on the sheet:
  //   CO: pin 14
  //   OVR: pin 13
  //   F0: pin 8
  //   F1: pin 9
  //   F2: pin 11
  //   F3: pin 12
  //   Cin: pin 15
  //   B0: pin 4
  //   A0: pin 3
  //   B1: pin 2
  //   A1: pin 1
  //   B2: pin 18
  //   A2: pin 19
  //   B3: pin 16
  //   A3: pin 17
  //   S0: pin 5
  //   S1: pin 6
  //   S2: pin 7
  //   VCC: pin 20, default 1
  //   GND: pin 10
endmodule

/* Test case Fairchild:
S0 S1 S2  Cin  A3 A2 A1 A0  B3 B2 B1 B0  F0 F1 F2 F3 OVR CO
# Clear
0  0  0   0    x  x  x  x   x  x  x  x   0  0  0  0   1   1
# B MINUS A
1  0  0   0    0  0  0  0   0  0  0  0   1  1  1  1   0   0
1  0  0   0    0  0  0  0   1  1  1  1   0  1  1  1   0   1
1  0  0   0    1  1  1  1   0  0  0  0   0  0  0  0   0   0
1  0  0   0    1  1  1  1   1  1  1  1   1  1  1  1   0   0
1  0  0   1    0  0  0  0   0  0  0  0   0  0  0  0   0   1
1  0  0   1    0  0  0  0   1  1  1  1   1  1  1  1   0   1
1  0  0   1    1  1  1  1   0  0  0  0   1  0  0  0   0   0
1  0  0   1    1  1  1  1   1  1  1  1   0  0  0  0   0   1
# A MINUS B
0  1  0   0    0  0  0  0   0  0  0  0   1  1  1  1   0   0
0  1  0   0    0  0  0  0   1  1  1  1   0  0  0  0   0   0
0  1  0   0    1  1  1  1   0  0  0  0   0  1  1  1   0   1
0  1  0   0    1  1  1  1   1  1  1  1   1  1  1  1   0   0
0  1  0   1    0  0  0  0   0  0  0  0   0  0  0  0   0   1
0  1  0   1    0  0  0  0   1  1  1  1   1  0  0  0   0   0
0  1  0   1    1  1  1  1   0  0  0  0   1  1  1  1   0   1
0  1  0   1    1  1  1  1   1  1  1  1   0  0  0  0   0   1
# A PLUS B
1  1  0   0    0  0  0  0   0  0  0  0   0  0  0  0   0   0
1  1  0   0    0  0  0  0   1  1  1  1   1  1  1  1   0   0
1  1  0   0    1  1  1  1   0  0  0  0   1  1  1  1   0   0
1  1  0   0    1  1  1  1   1  1  1  1   0  1  1  1   0   1
1  1  0   1    0  0  0  0   0  0  0  0   1  0  0  0   0   0
1  1  0   1    0  0  0  0   1  1  1  1   0  0  0  0   0   1
1  1  0   1    1  1  1  1   0  0  0  0   0  0  0  0   0   1
1  1  0   1    1  1  1  1   1  1  1  1   1  1  1  1   0   1
# A XOR B
0  0  1   x    0  0  0  0   0  0  0  0   0  0  0  0   0   0
0  0  1   x    0  0  0  0   1  1  1  1   1  1  1  1   0   0
0  0  1   0    1  1  1  1   0  0  0  0   1  1  1  1   0   0
0  0  1   x    1  1  1  1   1  1  1  1   0  0  0  0   1   1
0  0  1   1    1  1  1  1   0  0  0  0   1  1  1  1   1   1
# A OR B
1  0  1   x    0  0  0  0   0  0  0  0   0  0  0  0   0  0
1  0  1   x    0  0  0  0   1  1  1  1   1  1  1  1   0  0
1  0  1   x    1  1  1  1   0  0  0  0   1  1  1  1   0  0
1  0  1   0    1  1  1  1   1  1  1  1   1  1  1  1   0  0
1  0  1   1    1  1  1  1   1  1  1  1   1  1  1  1   1  1
# A AND B
0  1  1   x    0  0  0  0   0  0  0  0   0  0  0  0   1  1
0  1  1   x    0  0  0  0   1  1  1  1   0  0  0  0   0  0
0  1  1   x    1  1  1  1   0  0  0  0   0  0  0  0   1  1
0  1  1   0    1  1  1  1   1  1  1  1   1  1  1  1   0  0
0  1  1   1    1  1  1  1   1  1  1  1   1  1  1  1   1  1
# Preset
1  1  1   x    0  0  0  0   0  0  0  0   1  1  1  1   0  0
1  1  1   x    0  0  0  0   1  1  1  1   1  1  1  1   0  0
1  1  1   x    1  1  1  1   0  0  0  0   1  1  1  1   0  0
1  1  1   0    1  1  1  1   1  1  1  1   1  1  1  1   0  0
1  1  1   1    1  1  1  1   1  1  1  1   1  1  1  1   1  1
*/

/* Test case Add:
S0 S1 S2  Cin  A3 A2 A1 A0  B3 B2 B1 B0  CO F3 F2 F1 F0 
# A PLUS B
loop (a,16)
loop (b,16)
1  1  0   0    bits(4,a)    bits(4,b)    bits(5,a+b)    
1  1  0   1    bits(4,a)    bits(4,b)    bits(5,a+b+1)    
end loop
end loop
*/

/* Test case Sub:
S0 S1 S2  Cin  A3 A2 A1 A0  B3 B2 B1 B0  CO F3 F2 F1 F0
# A MINUS B
loop (a,16)
loop (b,16)
0  1  0   1    bits(4,a)    bits(4,b)  bits(1,~((a-b)>>4))    bits(4,a-b)    
0  1  0   0    bits(4,a)    bits(4,b)  bits(1,~((a-b-1)>>4))  bits(4,a-b-1)  
end loop
end loop
*/

/* Test case Sub Signed:
S0 S1 S2  Cin  A3 A2 A1 A0  B3 B2 B1 B0  F3 F2 F1 F0 OVR
# A MINUS B
loop (ua,16)
loop (ub,16)
let a = ua - 8;
let b = ub - 8;
let d = a - b;
let dc = a - b - 1;
0  1  0   1    bits(4,a)    bits(4,b)   bits(4,d)    (!(signExt(4,d)=d))
0  1  0   0    bits(4,a)    bits(4,b)   bits(4,dc)   (!(signExt(4,dc)=dc))
end loop
end loop
*/
