// Digital circuit 74266.dig as structural Verilog
// quad 2-input XNOR gate with open collector outputs
module _74266 (
  input  _1A,
  input  _1B,
  input  _2A,
  input  _2B,
  input  _3B,
  input  _3A,
  input  _4A,
  input  _4B,
  input  VCC,
  input  GND,
  output _1Y,
  output _2Y,
  output _3Y,
  output _4Y
);

  wire xor_1_out, xor_2_out, xor_3_out, xor_4_out;

  xor xor_1 (xor_1_out, _1A, _1B);
  xor xor_2 (xor_2_out, _2A, _2B);
  xor xor_3 (xor_3_out, _3A, _3B);
  xor xor_4 (xor_4_out, _4A, _4B);
  PowerSupply powersupply_1 (.VDD(VCC), .GND(GND));
  NFET nfet_1 (.G(xor_1_out), .D(_1Y), .S(1'b0));
  NFET nfet_2 (.G(xor_2_out), .D(_2Y), .S(1'b0));
  NFET nfet_3 (.G(xor_3_out), .D(_3Y), .S(1'b0));
  NFET nfet_4 (.G(xor_4_out), .D(_4Y), .S(1'b0));

  // Notes on the sheet:
  //   _1A: pin 1
  //   _1B: pin 2
  //   _1Y: pin 3
  //   _2A: pin 5
  //   _2B: pin 6
  //   _2Y: pin 4
  //   _3B: pin 9
  //   _3A: pin 8
  //   _3Y: pin 10
  //   _4A: pin 12
  //   _4B: pin 13
  //   _4Y: pin 11
  //   VCC: pin 14, default 1
  //   GND: pin 7
endmodule
