// Digital circuit or_with_fake_testcase.dig as structural Verilog
module or_with_fake_testcase (
  input  A,
  input  B,
  output PERMIT
);

  or or_1 (PERMIT, A, B);
endmodule

/* Test case fake:
A B PERMIT
0 0 0
0 1 1
1 0 1
1 1 1
*/
