// Digital circuit unconnected.dig as structural Verilog
module unconnected (
  input  A,
  input  B,
  output C,
  output S
);

  // And and_1 has open pins: In_1=A, In_2=B, out=open
  // XOr xor_1 has open pins: In_1=A, In_2=B, out=open
endmodule
